// Logisim project Lab2-Part2-6001-Thompson.circ as structural Verilog: 1 circuit, main circuit main
module main (
  input  W,
  input  X,
  input  Y,
  input  Z
);

  wire and_1_out, and_2_out, and_3_out, or_1_out;

  and and_1 (and_1_out, ~W, Y);  // AND_Gate
  and and_2 (and_2_out, ~X, Y, Z);  // AND_Gate
  and and_3 (and_3_out, ~W, ~X, Z);  // AND_Gate
  or or_1 (or_1_out, and_1_out, and_2_out, and_3_out);
  // Probe on or_1_out

  // Notes on the sheet:
  //   MIDN Joshua Thompson 206360
  //   Lab Part2
  //   Result
endmodule
