// Logisim project Project2-6001-Thompson.circ as structural Verilog: 1 circuit, main circuit main
module main (
  input  Clock,
  input  Reset
);

  wire and_1_out, and_2_out, and_3_out, and_4_out, and_5_out, and_6_out, and_7_out, and_8_out, and_9_out,
       and_10_out, and_11_out, and_12_out, and_13_out, and_14_out, and_15_out, and_16_out, or_1_out,
       or_2_out, or_3_out, or_4_out;
  wire [3:0] d_ff_4_q;

  D_Flip_Flop d_ff_1 (.clk(Clock), .D(or_1_out), .Q(d_ff_4_q[3]), .reset(Reset));  // open: Qn, preset, en
  D_Flip_Flop d_ff_2 (.clk(Clock), .D(or_2_out), .Q(d_ff_4_q[2]), .reset(Reset));  // open: Qn, preset, en
  D_Flip_Flop d_ff_3 (.clk(Clock), .D(or_3_out), .Q(d_ff_4_q[1]), .reset(Reset));  // open: Qn, preset, en
  D_Flip_Flop d_ff_4 (.clk(Clock), .D(or_4_out), .Q(d_ff_4_q[0]), .reset(Reset));  // open: Qn, preset, en
  // Probe on d_ff_4_q[3]
  // Probe on d_ff_4_q[1]
  // Probe on d_ff_4_q[2]
  // Probe on d_ff_4_q[0]
  Hex_Digit_Display hex_digit_display_1 (.value(d_ff_4_q));  // open: dp
  and and_1 (and_1_out, ~d_ff_4_q[3], ~d_ff_4_q[2], d_ff_4_q[1]);  // AND_Gate
  and and_2 (and_2_out, ~d_ff_4_q[3], d_ff_4_q[2], ~d_ff_4_q[1], d_ff_4_q[0]);  // AND_Gate
  and and_3 (and_3_out, d_ff_4_q[3], d_ff_4_q[2], ~d_ff_4_q[1], ~d_ff_4_q[0]);  // AND_Gate
  and and_4 (and_4_out, d_ff_4_q[3], ~d_ff_4_q[2], ~d_ff_4_q[1], d_ff_4_q[0]);  // AND_Gate
  and and_5 (and_5_out, d_ff_4_q[3], ~d_ff_4_q[2], ~d_ff_4_q[1]);  // AND_Gate
  and and_6 (and_6_out, d_ff_4_q[3], ~d_ff_4_q[2], ~d_ff_4_q[0]);  // AND_Gate
  and and_7 (and_7_out, ~d_ff_4_q[3], d_ff_4_q[2], d_ff_4_q[1]);  // AND_Gate
  and and_8 (and_8_out, d_ff_4_q[3], ~d_ff_4_q[2], ~d_ff_4_q[1], ~d_ff_4_q[0]);  // AND_Gate
  and and_9 (and_9_out, ~d_ff_4_q[3], d_ff_4_q[2], ~d_ff_4_q[1], ~d_ff_4_q[0]);  // AND_Gate
  and and_10 (and_10_out, ~d_ff_4_q[3], ~d_ff_4_q[2], d_ff_4_q[1]);  // AND_Gate
  and and_11 (and_11_out, ~d_ff_4_q[3], ~d_ff_4_q[2], d_ff_4_q[0]);  // AND_Gate
  and and_12 (and_12_out, ~d_ff_4_q[3], d_ff_4_q[1], d_ff_4_q[0]);  // AND_Gate
  and and_13 (and_13_out, ~d_ff_4_q[3], ~d_ff_4_q[2], d_ff_4_q[1], d_ff_4_q[0]);  // AND_Gate
  and and_14 (and_14_out, ~d_ff_4_q[3], d_ff_4_q[2], ~d_ff_4_q[1]);  // AND_Gate
  and and_15 (and_15_out, ~d_ff_4_q[3], ~d_ff_4_q[1], ~d_ff_4_q[0]);  // AND_Gate
  and and_16 (and_16_out, d_ff_4_q[3], ~d_ff_4_q[2], ~d_ff_4_q[0]);  // AND_Gate
  or or_1 (or_1_out, and_1_out, and_2_out, and_3_out, and_4_out);
  or or_2 (or_2_out, and_5_out, and_6_out, and_7_out);
  or or_3 (or_3_out, and_8_out, and_9_out, and_10_out, and_11_out, and_12_out);
  or or_4 (or_4_out, and_13_out, and_14_out, and_15_out, and_16_out);
  // Probe on or_1_out
  // Probe on or_2_out
  // Probe on or_3_out
  // Probe on or_4_out

  // Notes on the sheet:
  //   Q3
  //   Q2
  //   Q1
  //   Q0
  //   Q3
  //   Q2
  //   Q1
  //   Q0
  //   Q3'
  //   Q2'
  //   Q1'
  //   Q0'
endmodule
